# Fritzing sketch DevreSemasi (saved by Fritzing 0.9.3b)
breadboards: 2

parts:
  U1 = ESP8266 NodeMCU LoLin module
  LED1 = smd LED [color="Blue (470nm)" package="0603 [SMD]"]
  LED2 = smd LED [color="Green (560nm)" package="0603 [SMD]"]
  LED3 = smd LED [color="Red (633nm)" package="0603 [SMD]"]
  LED4 = smd LED [color="Red (633nm)" package="0603 [SMD]"]
  LED5 = smd LED [color="Red (633nm)" package="0603 [SMD]"]
  R1 = Resistor [tolerance=±5% resistance=220 package="0603 [SMD]"]
  R2 = Resistor [tolerance=±5% resistance=220 package="0603 [SMD]"]
  R3 = Resistor [tolerance=±5% resistance=220 package="0603 [SMD]"]
  R4 = Resistor [tolerance=±5% resistance=220 package="0603 [SMD]"]
  R5 = Resistor [tolerance=±5% resistance=220 package="0603 [SMD]"]
  R6 = Resistor [tolerance=±5% resistance=220 package="0603 [SMD]"]
  Mod1 = MQ-7 breakout
  DHT1 = Humidity and Temperature Sensor DHT11
  Part1 = Barometric Pressure Sensor - BMP180 Breakout (GY-68)
  J1 = Piezo Speaker

nets:
  N1: U1.D0, R6.Pin_0, DHT1.Data-signal
  N2: U1.D1, Part1.SCL
  N3: U1.D2, Part1.SDA
  N4: U1.D3, R4.Pin_1
  N5: U1.D4, R3.Pin_1
  3V3: U1.3V3, R6.Pin_1, DHT1.Vcc
  N6: U1.GND, LED1.cathode, LED2.cathode, DHT1.GND_1, J1.pin2
  N7: U1.D5, R1.Pin_1
  N8: U1.D6, R2.Pin_1
  N9: U1.D7, R5.Pin_1
  N10: U1.D8, J1.pin1
  N11: LED1.anode, R1.Pin_0
  N12: LED2.anode, R2.Pin_0
  N13: LED3.cathode, LED4.cathode, LED5.cathode, Mod1.DO, Part1.GND
  N14: LED3.anode, R4.Pin_0
  N15: LED4.anode, R3.Pin_0
  N16: LED5.anode, R5.Pin_0
  N17: Mod1.AO, Part1.VCC

custom parts:
  ESP8266 NodeMCU LoLin module: ESP8266 based NodeMCU
  MQ-7 breakout: MQ-5 gas sensor
  Humidity and Temperature Sensor DHT11: Digital relative humidity & temperature sensor DHT11
